# Fritzing sketch Schema (saved by Fritzing 0.9.2b)
breadboards: 1

parts:
  T1 = LM35 Temperature Sensor [package="TO92 [THT]"]
  U2 = TRANSISTOR_NPN_2 [part_number=BC337 package=to-92]
  D1 = Rectifier Diode [part_number=1N4007 package="300 mil [THT]"]
  R1 = Resistor [tolerance=±5% resistance=56k package=THT]
  R2 = Resistor [tolerance=±5% resistance=56k package=THT]
  U1 = TRANSISTOR_NPN [part_number=BC337 package=sot223]
  R3 = Resistor [tolerance=±5% resistance=10k package=THT]
  R4 = Resistor [tolerance=±5% resistance=10k package=THT]
  R5 = Resistor [tolerance=±5% resistance=10k package=THT]
  R6 = Resistor [tolerance=±5% resistance=10k package=THT]
  R7 = Resistor [tolerance=±5% resistance=10k package=THT]

nets:
  N1: T1.+Vs, U1.E
  ANALOG 0: T1.Vout
  GND: T1.GND, R2.Pin_1, R7.Pin_1
  3.3V: U2.C
  N2: U2.B, R3.Pin_1
  N3: U2.E, D1.anode
  N4: D1.cathode, R5.Pin_0
  ANALOG 1/E2: R1.Pin_0
  N5: R1.Pin_1, R2.Pin_0
  N6: U1.B, R4.Pin_1
  5V: U1.C
  DIGITAL 5: R3.Pin_0
  DIGITAL 4: R4.Pin_0
  N7: R5.Pin_1, R6.Pin_0
  ANALOG 2/E1: R6.Pin_1, R7.Pin_0
